# Fritzing sketch flashing railroad lights (saved by Fritzing 0.9.6b)
circuit board: 8.382cm x 6.12422cm

parts:
  D1 = Diode [package=diode-1n4148]
  D2 = Diode [package=diode-1n4148]
  C1 = Electrolytic Capacitor [capacitance=10μF voltage=35V package="0605 [SMD, electrolytic]"]
  R1 = Resistor [tolerance=±5% resistance=220 package="2010 [SMD]"]
  R3 = Resistor [tolerance=±10% resistance=47 package="1206 [SMD]"]
  R2 = Resistor [tolerance=±5% resistance=220 package="2512 [SMD]"]
  VCC3 = Battery block 9V
  U2 = 555 Timer [package="DIP8 [THT]"]

nets:
  N1: D1.A, VCC3.+, U2.Reset, U2.Vcc_Supply_Voltage
  N2: D1.C, R1.Pin_0
  N3: D2.A, R2.Pin_1
  N4: D2.C, C1.-, VCC3.-
  N5: C1.+, R3.Pin_1, U2.Trigger, U2.Threshold
  N6: R1.Pin_1, R3.Pin_0, R2.Pin_0, U2.Output
